# Fritzing sketch Medida Consumo (saved by Fritzing 0.9.3b)

parts:
  Componente1 = Arduino Sensor Shield v5.0
  U1 = 4-Channel 5v Relay Shield [package=relay-4ch5v10a]
  Componente2 = ACS712 Low Current Sensor Board v12
  M1 = DC Motor
  BATT1 = 3xAAA Switchable Battery Pack w/JST connector

nets:
  N1: Componente1.A5, Componente2.5V
  N2: Componente1.+5V#52, Componente1.D10, Componente1.D11, Componente1.+5V#105, Componente1.+5V#106, Componente1.+5V#108, U1.VCC, U1.IN4, U1.IN3
  N3: Componente1.D8, U1.IN1
  N4: Componente1.D9, U1.IN2
  N5: Componente1.GND#96, Componente1.GND#123, U1.GND
  N6: Componente1.GND#137, Componente2.GND
  N7: Componente1.+5V#143, Componente2.VO
  N8: U1.K4-Off, M1.pin_1
  N9: U1.K4-On, Componente2.IP-
  N10: Componente2.IP+, BATT1.NEG
  N11: M1.pin_2, BATT1.POS

custom parts:
  4-Channel 5v Relay Shield: 4 Channel 5v Relay Shield w. 2x SPD-06VDC-SD-C
  3xAAA Switchable Battery Pack w/JST connector: 3xAAA Switchable Battery Pack with JST connector
